# Fritzing sketch linus_v1_R2 (saved by Fritzing 0.9.3b)
breadboards: 1

parts:
  Parte2 = Motor Driver 1A Dual TB6612FNG
  S1 = Toggle Switch [package=THT]
  BATT1 = LiPoly Battery (1300mAh)
  S2 = Pushbutton [package="[THT]"]
  S3 = Pushbutton [package="[THT]"]
  M1 = DC Motor
  M2 = DC Motor
  Componente1 = Arduino Nano (Rev3.0) (ICSP)
  LED1 = LED - 3mm [color="Red (635nm)" package="3 mm [THT]"]
  R1 = Resistor [tolerance=±5% resistance=220 package=THT]

nets:
  GND: Parte2.GND, BATT1.negative, S2.Pin_1, S2.Pin_2, S3.Pin_1, S3.Pin_2, Componente1.GND, R1.Pin_0
  N1: Parte2.B01, M1.pin_1
  N2: Parte2.B02, M1.pin_2
  N3: Parte2.A02, M2.pin_1
  N4: Parte2.A01, M2.pin_2
  VCC: Parte2.VCC, Componente1.5V
  N5: Parte2.VM, S1.COM, Componente1.VIN
  N6: Parte2.PWMA, Componente1.D3
  N7: Parte2.AIN2, Componente1.D4
  N8: Parte2.AIN1, Componente1.D5
  N9: Parte2.STBY, Componente1.D6
  N10: Parte2.BIN1, Componente1.D7
  N11: Parte2.BIN2, Componente1.D8
  N12: Parte2.PWMB, Componente1.D9
  N13: S1.L1, BATT1.positive
  N14: S2.Pin_3, S2.Pin_4
  N15: S3.Pin_3, S3.Pin_4
  N16: Componente1.D0/RX, LED1.anode
  N17: LED1.cathode, R1.Pin_1

notes:
  Gnd Vcc Led  [1][2][3][4][5][6][7][8]

custom parts:
  LiPoly Battery (1300mAh): Lithium Ion Polymer Battery (1300mAh)
